// Logisim project and2.circ as structural Verilog: 1 circuit, main circuit main
module main (
  input  A,
  input  B,
  output Y
);

  // AND_Gate and_1: pin names not known; wires that end beside it: A, B, Y
endmodule
