// Logisim project arith.circ as structural Verilog: 1 circuit, main circuit main
module main (
  input  [1:0] A,
  input  [1:0] B,
  input  C,
  output [1:0] SUM,
  output CO,
  output [1:0] DIF,
  output BO,
  output GT,
  output EQ,
  output LT,
  output [1:0] NEG,
  output [1:0] MUL,
  output [1:0] MCO,
  output [1:0] SHF
);

  Adder #(.width(2)) adder_1 (.a(A), .b(B), .out(SUM), .cin(C), .cout(CO));
  Subtractor #(.width(2)) subtractor_1 (.a(A), .b(B), .out(DIF), .bin(C), .bout(BO));
  Comparator #(.width(2)) comparator_1 (.a(A), .b(B), .gt(GT), .eq(EQ), .lt(LT));
  Negator #(.width(2)) negator_1 (.in(A), .out(NEG));
  Multiplier #(.width(2)) multiplier_1 (.a(A), .b(B), .out(MUL), .cin(2'b10), .cout(MCO));
  Shifter #(.width(2), .shift("ar")) shifter_1 (.in(A), .\dist (C), .out(SHF));
endmodule
