// Logisim project counter.circ as structural Verilog: 1 circuit, main circuit main
module main (
  output TQ,
  output JQ,
  output SQ,
  output [1:0] CNT,
  output CRY,
  output [1:0] REG
);

  wire CLK, TN;

  Clock clock_1 (.out(CLK));
  // T_Flip_Flop t_ff_1: pin names not known; wires that end beside it: 1'b1, CLK
  J_K_Flip_Flop j_k_ff_1 (.reset(1'b1));  // open: J, clk, K, Q, Qn, preset, en
  // S_R_Flip_Flop s_r_ff_1: pin names not known; wires that end beside it: TQ, TN, CLK
  Counter #(.width(2)) counter_1 ();  // open: load, D, count, Q, carry, clk, clr
  Register #(.width(2)) register_1 ();  // open: D, en, Q, clk, clr
endmodule
