// Logisim project display.circ as structural Verilog: 1 circuit, main circuit main
module main (
  input  A,
  input  [3:0] H,
  input  S2,
  input  S1,
  input  S0,
  output OUT
);

  LED led_1 (.in(A));
  Hex_Digit_Display hex_digit_display_1 (.value(H));  // open: dp
  _7_Segment_Display u_7_segment_display_1 (.f(S0), .a(S1), .b(S2));  // open: g, e, d, c, dp

  assign OUT = A;
endmodule
