// Logisim project mixed.circ as structural Verilog: 1 circuit, main circuit main
module main (
  input  A,
  input  B,
  input  C,
  output P,
  output Q
);

  wire nor_1_out, xor_1_p3;

  // XOR_Gate xor_1: pin names not known; wires that end beside it: A, B, xor_1_p3
  nor nor_1 (nor_1_out, C, C, C);
  nand nand_1 (P, xor_1_p3, xor_1_p3);
  not not_1 (Q, nor_1_out);
endmodule
