// Logisim project plexer.circ as structural Verilog: 1 circuit, main circuit main
module main (
  input  [1:0] A,
  input  [1:0] B,
  input  S,
  input  E,
  output [1:0] MUX,
  output [1:0] D0,
  output [1:0] D1,
  output C0,
  output C1
);

  Multiplexer #(.width(2)) multiplexer_1 (.in0(A), .in1(B), .out(MUX), .sel(S));  // open: en
  Demultiplexer #(.width(2)) demultiplexer_1 (.out0(D0), .out1(D1), .in(A), .sel(S));  // open: en
  Decoder decoder_1 (.out0(C0), .out1(C1), .sel(S), .en(E));
endmodule
