// Logisim project poke.circ as structural Verilog: 1 circuit, main circuit main
module main (
  output B,
  output S1,
  output S2
);

  Button button_1 (.out(B));
  // DipSwitch #(.number(2)) dipswitch_1: pin names not known; wires that end beside it: S1, S2
endmodule
