// Logisim project shift.circ as structural Verilog: 1 circuit, main circuit main
module main (
  output Q1,
  output Q2
);

  wire clock_1_out, d_ff_1_p1;

  Clock clock_1 (.out(clock_1_out));
  // D_Flip_Flop d_ff_1: pin names not known; wires that end beside it: d_ff_1_p1, clock_1_out
  // D_Flip_Flop d_ff_2: pin names not known; wires that end beside it: Q1, clock_1_out
endmodule
