// Logisim project splitter.circ as structural Verilog: 1 circuit, main circuit main
module main (
  input  A,
  input  B,
  input  [1:0] D,
  input  C,
  output [1:0] S,
  output D0,
  output [1:0] E,
  output D1
);

  assign E = {{1{1'b1}}, C};  // Bit_Extender bit_extender_1

  assign D0 = D[0];
  assign D1 = D[1];
  assign S = {B, A};
endmodule
