// Logisim project subcircuit.circ as structural Verilog: 3 circuits, main circuit main
module half (
  input  a,
  input  b,
  output s,
  output c
);

  xor xor_1 (s, a, b);
  and and_1 (c, a, b);
endmodule

module full (
  input  A,
  input  B,
  input  CI,
  output S,
  output CO
);

  wire c, c2, s1;

  half half_1 (.a(A), .b(B), .s(s1), .c(c));
  half half_2 (.a(s1), .b(CI), .s(S), .c(c2));
  or or_1 (CO, c, c2);
endmodule

module main (
  input  A,
  input  B,
  input  CI,
  output S,
  output CO
);

  full full_1 (.A(A), .B(B), .CI(CI), .S(S), .CO(CO));
endmodule
